# Fritzing sketch Skematik (saved by Fritzing 0.9.5d)

parts:
  BATERAI_7_4 = Battery
  S3 = Round Pushbutton
  Jack_Charger = Power Jack [package=power_jack_pth_lock]
  Speaker = SPEAKER [package=pcb_mount_speaker]
  Mic_INMP441 = INMP441
  Ampli_Max98357A = Adafruit MAX98357A I2S 3W Class D Amplifier [part_number="Adafruit #3006"]
  C1 = Capacitor Polarized [package=nippon_f80]
  Kapasitor_1000uF = Capacitor Polarized [package=nippon_f80]
  R2 = Resistor [tolerance=±5% resistance=220 package=THT]
  Step_Down_DC = SBX DSUN [package=THT]
  ESP32 = DOIT Esp32 DevKit v1 (30 pins long, 11 pins width) [part_number=ESP32S-PIN30]
  ESP32_2 = DOIT Esp32 DevKit v1 (30 pins long, 11 pins width) [part_number=ESP32S-PIN30]
  Switch_On/Off1 = SPST Switch [package=r_sw_th]
  Kapasitor_470uF = Electrolytic Capacitor [capacitance=1µF package="100 mil [THT, electrolytic]"]

nets:
  N1: BATERAI_7_4.-, Jack_Charger.GNDBREAK
  N2: BATERAI_7_4.+, Jack_Charger.GND, Step_Down_DC.+VIN
  GND: S3.leg0, Mic_INMP441.L/R, Mic_INMP441.GND, Ampli_Max98357A.GND, Ampli_Max98357A.GAIN, C1.-, Kapasitor_1000uF.-, Step_Down_DC.GND, ESP32.GND, ESP32_2.GND
  N3: S3.leg1, ESP32.D2
  N4: Speaker.+, Ampli_Max98357A.VO-, Kapasitor_470uF.-
  N5: Speaker.-, Ampli_Max98357A.VO+, Kapasitor_470uF.+
  N6: Mic_INMP441.WS, ESP32.D25
  N7: Mic_INMP441.SCK, ESP32.D26
  N8: Mic_INMP441.SD, ESP32.D21
  VDD: Mic_INMP441.VDD, R2.Pin_1, ESP32.3V3
  VIN: Ampli_Max98357A.VIN, C1.+, ESP32.VIN, ESP32_2.VIN, Switch_On/Off1.O
  N9: Ampli_Max98357A.DIN, ESP32_2.D27
  N10: Ampli_Max98357A.BCLK, ESP32_2.D26
  N11: Ampli_Max98357A.LRCLK, ESP32_2.D25
  N12: Kapasitor_1000uF.+, R2.Pin_0
  N13: Step_Down_DC.+VOUT, Switch_On/Off1.P

custom parts:
  INMP441: This is a simple breakout board for the INMP441 I2S MEMS microphone.
  Adafruit MAX98357A I2S 3W Class D Amplifier: Listen to this good news - we now have an all in one digital audio amp breakout board that works incredibly well with the Raspberry Pi! If you're looking for an easy and low cost way to get you digital sound files bumpin' then the MAX08357 I2S Amp Breakout is for you. It takes standard I2S digital audio input and, not only decodes it into analog, but also amplifies it directly into a speaker.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
  SBX DSUN: SBX DSUN input voltage 4.5 - 28V DC output voltage .8v to 20VDC (step down converter) Output current 3A max
  DOIT Esp32 DevKit v1 (30 pins long, 11 pins width): The DOIT Esp32 DevKit v1 is one of the development board created by DOIT to evaluate the ESP-WROOM-32 module. It is based on the ESP32 microcontroller that boasts Wifi, Bluetooth, Ethernet and Low Power support all in a single chip. (vanepp) made breadboard work, adjusted pin numbering and labels and reduced size of schematic and cleaned up pcb. This chip is 30pins long (2 x15) and 11 pins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
